# Fritzing sketch all_chips (saved by Fritzing 0.9.10b)
breadboards: 1

parts:
  74HC1 = 74HC181 - 4-bit arithmetic logic unit [package="DIP (Dual Inline) [THT]"]
  74HC2 = 74HC161 - Presettable synchronous 4-bitbinary counter; asynchronous reset [package="DIP (Dual Inline) [THT]"]
  74HC3 = 74HC151 - 8-input multiplexer [package="DIP (Dual Inline) [THT]"]
  74HC4 = 74HC139 - Dual 2-to-4 linedecoder/demultiplexer [package="DIP (Dual Inline) [THT]"]
  74HC5 = 74HC138 - 3-to-8 line decoder/demultiplexer; inverting [package="DIP (Dual Inline) [THT]"]
  74HC9 = 74HC163 - Presettable synchronous 4-bitbinary counter; synchronous reset [package="DIP (Dual Inline) [THT]"]
  74HC10 = 74HC595 - 8-bit serial-in, serial or parallel-outshift register with output latches;3-state [package="DIP (Dual Inline) [THT]"]
  74HC18 = 74HC245 - Octal bus tranceiver; 3-state [package="DIP (Dual Inline) [THT]"]
  74HC19 = 74HC273 - Octal D-type flip-flop with reset;positive-edge trigger [package="DIP (Dual Inline) [THT]"]
  74HC20 = 74HC283 - 4-bit binary full adder with fast carry [package="DIP (Dual Inline) [THT]"]
  74HC22 = 74HC4078 - 8-INPUT NOR/OR GATE [package="DIP (Dual Inline) [THT]"]
  74HC21 = 74HC299 - 8-bit universal shift register; 3-state [package="DIP (Dual Inline) [THT]"]
  74HC17 = 74HC00 - Quad 2-input NAND gate [package="DIP (Dual Inline) [THT]"]
  74HC16 = 74HC02 - Quad 2-input NOR gate [package="DIP (Dual Inline) [THT]"]
  74HC15 = 74HC04 - Hex Inverter [package="DIP (Dual Inline) [THT]"]
  74HC11 = 74HC06 - Hex Inverter buffer/driver [package="DIP (Dual Inline) [THT]"]
  74HC14 = 74HC08 - Quad 2-input AND gate [package="DIP (Dual Inline) [THT]"]
  74HC13 = 74HC10 - Triple 3-input NAND gate [package="DIP (Dual Inline) [THT]"]
  74HC12 = 74HC11 - Triple 3-input AND gate [package="DIP (Dual Inline) [THT]"]
  74HC8 = 74HC32 - Quad 2-input OR gate [package="DIP (Dual Inline) [THT]"]
  74HC7 = 74HC74 - Dual D-type flip-flop with set andreset; positive-edge trigger [package="DIP (Dual Inline) [THT]"]
  74HC6 = 74HC86 - Quad 2-input EXCLUSIVE-OR gate [package="DIP (Dual Inline) [THT]"]

nets:
  N1: 74HC1.B(bar)0, 74HC1.Vcc
  N2: 74HC1.A(bar)0, 74HC1.A(bar)1
  N3: 74HC1.S3, 74HC1.B(bar)1
  N4: 74HC1.S2, 74HC1.A(bar)2
  N5: 74HC1.S1, 74HC1.B(bar)2
  N6: 74HC1.S0, 74HC1.A(bar)3
  N7: 74HC1.Cn, 74HC1.B(bar)3
  N8: 74HC1.M, 74HC1.G(bar)
  N9: 74HC1.F(bar)0, 74HC1.Cn_+_4
  N10: 74HC1.F(bar)1, 74HC1.P(bar)
  N11: 74HC1.F(bar)2, 74HC1.A_=_B
  N12: 74HC1.GND, 74HC1.F(bar)3
  N13: 74HC2.MR(bar), 74HC2.Vcc
  N14: 74HC2.CP, 74HC2.TC
  N15: 74HC2.D0, 74HC2.Q0
  N16: 74HC2.D1, 74HC2.Q1
  N17: 74HC2.D2, 74HC2.Q2
  N18: 74HC2.D3, 74HC2.Q3
  N19: 74HC2.CEP, 74HC2.CET
  N20: 74HC2.GND, 74HC2.PE(bar)
  N21: 74HC3.I3, 74HC3.Vcc
  N22: 74HC3.I2, 74HC3.I4
  N23: 74HC3.I1, 74HC3.I5
  N24: 74HC3.I0, 74HC3.I6
  N25: 74HC3.Y, 74HC3.I7
  N26: 74HC3.Y(bar), 74HC3.S0
  N27: 74HC3.E(bar), 74HC3.S1
  N28: 74HC3.GND, 74HC3.S2
  N29: 74HC4.1E(bar), 74HC4.Vcc, 74HC6.1B
  N30: 74HC4.1A0, 74HC4.2E(bar), 74HC6.1Y
  N31: 74HC4.1A1, 74HC4.2A0, 74HC6.2A
  N32: 74HC4.1Y(bar)0, 74HC4.2A1, 74HC6.2B
  N33: 74HC4.1Y(bar)1, 74HC4.2Ybar(0), 74HC6.2Y
  N34: 74HC4.1Y(bar)2, 74HC4.2Y(bar)1, 74HC6.GND
  N35: 74HC4.1Y(bar)3, 74HC4.2Y(bar)2
  N36: 74HC4.GND, 74HC4.2Y(bar)3
  N37: 74HC5.A0, 74HC5.Vcc, 74HC7.1R(bar)D
  N38: 74HC5.A1, 74HC5.Y(bar)0, 74HC7.1D
  N39: 74HC5.A2, 74HC5.Y(bar)1, 74HC7.1CP
  N40: 74HC5.E(bar)1, 74HC5.Y(bar)2, 74HC7.1S(bar)D
  N41: 74HC5.E(bar)2, 74HC5.Y(bar)3, 74HC7.1Q
  N42: 74HC5.E3, 74HC5.Y(bar)4, 74HC7.1Q(bar)
  N43: 74HC5.Y(bar)7, 74HC5.Y(bar)5, 74HC7.GND
  N44: 74HC5.GND, 74HC5.Y(bar)6
  N45: 74HC9.MR_(bar), 74HC9.Vcc
  N46: 74HC9.CP, 74HC9.TC
  N47: 74HC9.D0, 74HC9.Q0
  N48: 74HC9.D1, 74HC9.Q1
  N49: 74HC9.D2, 74HC9.Q2
  N50: 74HC9.D3, 74HC9.Q3
  N51: 74HC9.CEP, 74HC9.CET
  N52: 74HC9.GND, 74HC9.PE(bar)
  GND: 74HC10.Q1, 74HC10.Q3, 74HC10.Q4, 74HC10.Q5, 74HC10.Q6, 74HC10.Q7, 74HC18.A1, 74HC18.A2, 74HC18.A3, 74HC18.A4, 74HC18.A5, 74HC18.A7, 74HC18.GND, 74HC19.MR(bar), 74HC19.Q0, 74HC19.D1, 74HC19.Q1, 74HC19.Q2, 74HC19.D2, 74HC19.D3, 74HC19.GND, 74HC20.Sigma2, 74HC20.B2, 74HC20.A2, 74HC20.A1, 74HC20.B1, 74HC20.Cin, 74HC20.GND, 74HC22.Y, 74HC22.A, 74HC22.B, 74HC22.C, 74HC22.N.C., 74HC22.GND, 74HC21.OE1(bar), 74HC21.OE2(bar), 74HC21.I/O6, 74HC21.I/O4, 74HC21.I/O2, 74HC21.Q0, 74HC21.MR(bar), 74HC21.GND
  VCC: 74HC17.1A, 74HC17.Vcc, 74HC7.Vcc
  N53: 74HC17.1B, 74HC17.4B, 74HC7.2R(bar)D
  N54: 74HC17.1Y, 74HC17.4A, 74HC7.2D
  N55: 74HC17.2A, 74HC17.4Y, 74HC7.2CP
  N56: 74HC17.2B, 74HC17.3B, 74HC7.2S(bar)D
  N57: 74HC17.2Y, 74HC17.3A, 74HC7.2Q
  N58: 74HC17.GND, 74HC17.3Y, 74HC7.2Q(bar)
  VCC_2: 74HC16.1Y, 74HC16.Vcc, 74HC6.Vcc
  N59: 74HC16.1A, 74HC16.4Y, 74HC6.4B
  N60: 74HC16.1B, 74HC16.4B, 74HC6.4A
  N61: 74HC16.2Y, 74HC16.4A, 74HC6.4Y
  N62: 74HC16.2A, 74HC16.3Y, 74HC6.3B
  N63: 74HC16.2B, 74HC16.3B, 74HC6.3A
  N64: 74HC16.GND, 74HC16.3A, 74HC6.3Y
  N65: 74HC15.1A, 74HC15.Vcc
  N66: 74HC15.1B, 74HC15.6A
  N67: 74HC15.2A, 74HC15.6Y
  N68: 74HC15.2Y, 74HC15.5A
  N69: 74HC15.3A, 74HC15.5Y
  N70: 74HC15.3Y, 74HC15.4A
  N71: 74HC15.GND, 74HC15.4Y
  N72: 74HC11.1A, 74HC11.Vcc
  N73: 74HC11.1B, 74HC11.6A
  N74: 74HC11.2A, 74HC11.6Y
  N75: 74HC11.2Y, 74HC11.5A
  N76: 74HC11.3A, 74HC11.5Y
  N77: 74HC11.3Y, 74HC11.4A
  N78: 74HC11.GND, 74HC11.4Y
  N79: 74HC14.1A, 74HC14.Vcc
  N80: 74HC14.1B, 74HC14.4Y
  N81: 74HC14.1Y, 74HC14.4B
  N82: 74HC14.2A, 74HC14.4A
  N83: 74HC14.2B, 74HC14.3Y
  N84: 74HC14.2Y, 74HC14.3B
  N85: 74HC14.GND, 74HC14.3A
  N86: 74HC13.1A, 74HC13.Vcc
  N87: 74HC13.1B, 74HC13.1C
  N88: 74HC13.2A, 74HC13.1Y
  N89: 74HC13.2B, 74HC13.3C
  N90: 74HC13.2C, 74HC13.3B
  N91: 74HC13.2Y, 74HC13.3A
  N92: 74HC13.GND, 74HC13.3Y
  N93: 74HC12.1A, 74HC12.Vcc
  N94: 74HC12.1B, 74HC12.1C
  N95: 74HC12.2A, 74HC12.1Y
  N96: 74HC12.2B, 74HC12.3C
  N97: 74HC12.2C, 74HC12.3B
  N98: 74HC12.2Y, 74HC12.3A
  N99: 74HC12.GND, 74HC12.3Y
  N100: 74HC8.1A, 74HC8.Vcc
  N101: 74HC8.1B, 74HC8.4B
  N102: 74HC8.1Y, 74HC8.4A
  N103: 74HC8.2A, 74HC8.4Y
  N104: 74HC8.2B, 74HC8.3B
  N105: 74HC8.2Y, 74HC8.3A
  N106: 74HC8.GND, 74HC8.3Y

custom parts:
  74HC181 - 4-bit arithmetic logic unit: The 74HC/HCT181 are high-speed Si-gate CMOS devicesand are pin compatible with low power Schottky TTL(LSTTL). They are specified in compliance with JEDECstandard no. 7A.The 74HC/HCT181 are 4-bit high-speed parallelArithmetic Logic Units (ALU). Controlled by the fourfunction select inputs (S0to S3) and the mode control input(M), they can perform all the 16 possible logic operationsor 16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
  74HC161 - Presettable synchronous 4-bitbinary counter; asynchronous reset: The 74HC/HCT161 are high-speed Si-gate CMOS devicesand are pin compatible with low power Schottky TTL(LSTTL). They are specified in compliance with JEDECstandard no. 7A.The 74HC/HCT161 are synchronous presettable binarycounters which feature an internal look-ahead carry andcan be used for high-speed counting.Synchronous operation is provided by having all flip-flopsclocked simultaneously on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
  74HC151 - 8-input multiplexer: The 74HC/HCT151 are high-speed Si-gate CMOS devices and are pin compatible with low power Schottky TTL (LSTTL).They are specified in compliance with JEDEC standard no. 7A.
  74HC139 - Dual 2-to-4 linedecoder/demultiplexer: The 74HC/HCT139 are high-speed Si-gate CMOS devicesand are pin compatible with low power Schottky TTL(LSTTL). It is specified in compliance with JEDECstandard no. 7A.The 74HC/HCT139 are high-speed, dual 2-to-4 linedecoder/multiplexers. This device has two independentdecoders, each accepting two binary weighted inputs(nA0and nA1) and providing four mutually exclusive activeLOW outputs (nY0 to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
  74HC138 - 3-to-8 line decoder/demultiplexer; inverting: The 74HC/HCT138 are high-speed Si-gate CMOS devicesand are pin compatible with low power Schottky TTL(LSTTL). They are specified in compliance with JEDECstandard no. 7A.The 74HC/HCT138 decoders accept three binaryweighted address inputs (A0, A1, A2) and when enabled,provide 8 mutually exclusive active LOW outputs (Y0toY7).
  74HC163 - Presettable synchronous 4-bitbinary counter; synchronous reset: The 74HC/HCT163 are high-speed Si-gate CMOS devicesand are pin compatible with low power Schottky TTL(LSTTL). They are specified in compliance with JEDECstandard no. 7A.
  74HC595 - 8-bit serial-in, serial or parallel-outshift register with output latches;3-state: The 74HC/HCT595 are high-speed Si-gate CMOS devicesand are pin compatible with low power Schottky TTL(LSTTL). They are specified in compliance with JEDECstandard no. 7A.The 74HC/HCT595 is an 8-stage serial shift register with astorage register and 3-state outputs. The shift register andstorage register have separate clocks.Data is shifted on the positive-going transitions of theSH_CP input.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
  74HC245 - Octal bus tranceiver; 3-state: The 74HC245; 74HCT245 is a high-speed Si-gate CMOS device and is pin compatiblewith Low-Power Schottky TTL (LSTTL).The 74HC245; 74HCT245 is an octal transceiver featuring non-inverting 3-state buscompatible outputs in both send and receive directions. The 74HC245; 74HCT245features an output enable input (OE) for easy cascading and a send/receive input (DIR)for direction control.OE controls the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
  74HC273 - Octal D-type flip-flop with reset;positive-edge trigger: The 74HC/HCT273 are high-speed Si-gate CMOS devicesand are pin compatible with low power Schottky TTL(LSTTL). They are specified in compliance with JEDECstandard no. 7A.The 74HC/HCT273 have eight edge-triggered, D-typeflip-flops with individual D inputs and Q outputs. Thecommon clock (CP) and master reset (MR) inputs load andreset (clear) all flip-flops simultaneouslya.
  74HC283 - 4-bit binary full adder with fast carry: The 74HC/HCT283 are high-speed Si-gate CMOS devicesand are pin compatible with low power Schottky TTL(LSTTL). They are specified in compliance with JEDECstandard no. 7A.The 74HC/HCT283 add two 4-bit binary words (An plus Bn)plus the incoming carry.
  74HC4078 - 8-INPUT NOR/OR GATE: The M74HC4078 is an high speed CMOS 8-INPUT NOR/OR GATE fabricated with silicon gate C2MOS technology.
  74HC299 - 8-bit universal shift register; 3-state: The 74HC/HCT299 are high-speed Si-gate CMOS devicesand are pin compatible with low power Schottky TTL(LSTTL). They are specified in compliance with JEDECstandard no. 7A.The 74HC/HCT299 contain eight edge-triggered D-typeflip-flops and the interstage logic necessary to performsynchronous shift-right, shift-left, parallel load and holdoperations. The type of operation is determined by themode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
  74HC00 - Quad 2-input NAND gate: The 74HC00; 74HCT00 are high-speed Si-gate CMOS devices that comply with JEDEC standard no. 7A. They are pin compatible with Low-power Schottky TTL (LSTTL).The 74HC00; 74HCT00 provides a quad 2-input NAND function.
  74HC02 - Quad 2-input NOR gate: The 74HC/HCT02 are high-speed Si-gate CMOS devices and are pin compatible with low power Schottky TTL (LSTTL). They are specified in compliance with JEDEC standard no. 7A. The 74HC/HCT02 provide the 2-input NOR function.
  74HC04 - Hex Inverter: The 74HC/HCT04 are high-speed Si-gate CMOS devicesand are pin compatible with low power Schottky TTL(LSTTL). They are specified in compliance with JEDECstandard no. 7A. The 74HC/HCT04 provide six invertingbuffers.
  74HC06 - Hex Inverter buffer/driver: These TTL hex inverter buffers/drivers feature high-voltage open-collector outputs for interfacing with high-level circuits (such as MOS) or for driving high-current loads (such as lamps or relays), and also are characterized for use as inverter buffers for driving TTL in
  74HC08 - Quad 2-input AND gate: The 74HC/HCT08 are high-speed Si-gate CMOS devicesand are pin compatible with low power Schottky TTL(LSTTL). They are specified in compliance with JEDECstandard no. 7A. The 74HC/HCT08 provide the 2-inputAND function.
  74HC10 - Triple 3-input NAND gate: The 74HC/HCT10 are high-speed Si-gate CMOS devices and are pin compatible with low power Schottky TTL (LSTTL).They are specified in compliance with JEDEC standard no. 7A.The 74HC/HCT10 provide the 3-input NAND function
  74HC11 - Triple 3-input AND gate: The 74HC/HCT11 are high-speed Si-gate CMOS devices and are pin compatible with low power Schottky TTL (LSTTL).They are specified in compliance with JEDEC standard no. 7A. The 74HC/HCT11 provide the 3-input AND function.
  74HC32 - Quad 2-input OR gate: The 74HC/HCT32 are high-speed Si-gate CMOS devicesand are pin compatible with low power Schottky TTL(LSTTL). They are specified in compliance with JEDECstandard no. 7A.
  74HC74 - Dual D-type flip-flop with set andreset; positive-edge trigger: The 74HC/HCT74 is a high-speed Si-gate CMOS deviceand is pin compatible with low power Schottky TTL(LSTTL). They are specified in compliance with JEDECstandard no. 7A.
  74HC86 - Quad 2-input EXCLUSIVE-OR gate: The 74HC/HCT86 are high-speed Si-gate CMOS devicesand are pin compatible with low power Schottky TTL(LSTTL). They are specified in compliance with JEDECstandard no. 7A.The 74HC/HCT86 provide the EXCLUSIVE−OR function.
